# Fritzing sketch fritzing-wiring-plan (saved by Fritzing 1.0.2b)
breadboards: 1

parts:
  Composant2 = Adafruit TCA9548A
  Composant4 = Adafruit AHT20 Temperature and Humidity Sensor [part_number="Adafruit #4566"]
  Composant5 = Adafruit AHT20 Temperature and Humidity Sensor [part_number="Adafruit #4566"]
  Composant6 = Adafruit AHT20 Temperature and Humidity Sensor [part_number="Adafruit #4566"]
  J1 = Generic male header - 4 pins [form="♂ (male)" package=THT]
  J2 = Generic male header - 4 pins [form="♂ (male)" package=THT]
  F1 = Fan - 4 wire [package=THT]
  F2 = Fan - 4 wire [package=THT]
  F3 = Fan - 4 wire [package=THT]
  F4 = Fan - 4 wire [package=THT]
  R1 = Resistor [tolerance=±5% resistance=10k package="0805 [SMD]"]
  R2 = Resistor [tolerance=±5% resistance=10k package="0805 [SMD]"]
  R3 = Resistor [tolerance=±5% resistance=10k package="0805 [SMD]"]
  F5 = Fan - 4 wire [package=THT]
  R5 = Resistor [tolerance=±5% resistance=10k package="0805 [SMD]"]
  R6 = Resistor [tolerance=±5% resistance=10k package="0805 [SMD]"]
  L1 = Solenoid
  Composant7 = Adafruit AHT20 Temperature and Humidity Sensor [part_number="Adafruit #4566"]
  F6 = Fan - 4 wire [package=THT]
  F7 = Fan - 4 wire [package=THT]
  R7 = Resistor [tolerance=±5% resistance=10k package="0805 [SMD]"]
  R8 = Resistor [tolerance=±5% resistance=10k package="0805 [SMD]"]
  M1 = BTS7960
  Composant1 = Arduino Mega 2560 (Rev3)
  BULB3 = Incandescent light bulb small [package="bulb sm"]
  BULB4 = Incandescent light bulb small [package="bulb sm"]

nets:
  N1: Composant2.2SDA, Composant7.SDA
  N2: Composant2.2SCL, Composant7.SCL
  N3: Composant2.3SDA, Composant6.SDA
  N4: Composant2.3SCL, Composant6.SCL
  N5: Composant2.4SDA, Composant5.SDA
  N6: Composant2.4SCL, Composant5.SCL
  N7: Composant2.5SDA, Composant4.SDA
  N8: Composant2.5SCL, Composant4.SCL
  VCC: Composant2.VCC, Composant4.VCC, J1.VCC, J2.VCC, R1.Pin_0, R2.Pin_0, R3.Pin_0, R5.Pin_0, R6.Pin_0, R7.Pin_0, R8.Pin_0, M1.pin7, Composant1.5V
  GND: Composant2.GND, Composant4.GND, J1.GND, J2.GND, M1.pin8, Composant1.GND
  N9: Composant2.INPUTSDA, Composant1.D20/SDA
  N10: Composant2.INPUTSCL, Composant1.D21/SCL
  N11: J1.Z-C, J2.Z-C, Composant1.D18/TX1
  N12: J1.PWM, Composant1.D6_PWM
  N13: J1.L-_IN, J2.L-_IN
  N14: J1.L-_OUT, BULB3.1
  N15: J1.N#6, J2.N#6
  N16: J1.N#7, BULB3.2
  N17: J2.PWM, Composant1.D7_PWM
  N18: J2.L-_OUT, BULB4.1
  N19: J2.N#7, BULB4.2
  N20: F1.PWM, R5.Pin_1, Composant1.D41
  N21: F1.Tach, Composant1.D45
  N22: F2.PWM, R1.Pin_1, Composant1.D43
  N23: F2.Tach, Composant1.D5_PWM
  N24: F3.PWM, R3.Pin_1, Composant1.D42
  N25: F3.Tach, Composant1.D2_PWM
  N26: F4.PWM, R2.Pin_1, Composant1.D51
  N27: F4.Tach, Composant1.D3_PWM
  N28: F5.PWM, R6.Pin_1, Composant1.D47
  N29: F5.Tach, Composant1.D44
  N30: L1.pin1, M1.pin12
  N31: L1.pin2, M1.pin11
  N32: F6.PWM, R7.Pin_1, Composant1.D38
  N33: F7.PWM, R8.Pin_1, Composant1.D40
  N34: M1.pin1, Composant1.D9_PWM
  N35: M1.pin2, Composant1.D10_PWM
  N36: M1.pin3, Composant1.D48
  N37: M1.pin4, Composant1.D49
  N38: M1.pin5, Composant1.A0
  N39: M1.pin6, Composant1.A1

notes:
  (f1BG) fans Chauffage bas gauche
  (F6BC) fan humidité bas
  (F5EXT) fan entrée d'air
  (F4HG) fan chauffage haut
  (F7HD) fan humidité haut
  (T5) Temp-Humid. bot-left
  (T4) Temp-Humid. bot-Right
  (T3) Temp-Humid. Top
  (botDimmer) Dimmer lumières bas 6 x 100w
  (topDimmer) Dimmer lumière haut 2 x 100w
  (T)Multiplexer
  10kΩ
  12 VDC
  attachInterrupt
  Linear actuator
  (T2) Temp-Humid. ext.
  120 VAC
  TCA9548A
  Temp & humidity
  AHT20
  (f2BD) fans Chauffage bas droit
  (f3BC) fans Chauffage bas centre
  Vers PWM pins
  (M) BTS7960

custom parts:
  Adafruit TCA9548A: You just found the perfect I2C sensor, and you want to wire up two or three or more of them to your Arduino when you realize "Uh oh, this chip has a fixed I2C address, and from what I know about I2C, you cannot have two devices with the same address on the same SDA/SCL pins!" Are you out of luck? You would be, if you didn't have this ultra-cool TCA9548A 1-to-8 I2C multiplexer! Finally, a way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
  Adafruit AHT20 Temperature and Humidity Sensor: The AHT20 is a nice but inexpensive temperature and humidity sensor from the same folks that brought us the DHT22. You can take sensor readings as often as you like, and it uses standard I2C so its super easy to use with any Arduino or Linux/Raspberry Pi board. This sensor has a typical accuracy of +- 2% relative humidity, and +-0.3 °C. There is only one I2C address so its not a good option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
  Generic male header - 4 pins: Generic male header
  Fan - 4 wire: Fan, 4 wire with tach.
  BTS7960: BTS7960 43A Peak Power H-Bridge PWM Motor Driver
